// Logisim project Pipelined_CPU.circ as structural Verilog
module _16_bit_register_file (
  input  Reset,
  input  [2:0] Read_Reg_1,
  input  [2:0] Read_Reg_2,
  input  Write,
  input  [2:0] Write_Reg_Destination,
  input  [15:0] Write_Data,
  output [15:0] Read_Reg_1_Output,
  output [15:0] Read_Reg_2_Output
);

  wire demultiplexer_1_out0, demultiplexer_1_out1, demultiplexer_1_out2, demultiplexer_1_out3,
       demultiplexer_1_out4, demultiplexer_1_out5, demultiplexer_1_out6, demultiplexer_1_out7;
  wire [15:0] r0_q, r1_q, r2_q, r3_q, r4_q, r5_q, r6_q;

  Demultiplexer #(.select(3)) demultiplexer_1 (
    .out0(demultiplexer_1_out0), .out1(demultiplexer_1_out1), .out2(demultiplexer_1_out2),
    .out3(demultiplexer_1_out3), .out4(demultiplexer_1_out4), .out5(demultiplexer_1_out5),
    .out6(demultiplexer_1_out6), .out7(demultiplexer_1_out7), .in(Write), .sel(Write_Reg_Destination));  // open: en
  Register #(.width(16)) r0 (.D(Write_Data), .Q(r0_q), .clk(demultiplexer_1_out0), .clr(Reset));  // open: en
  Register #(.width(16)) r1 (.D(Write_Data), .Q(r1_q), .clk(demultiplexer_1_out1), .clr(Reset));  // open: en
  Register #(.width(16)) r2 (.D(Write_Data), .Q(r2_q), .clk(demultiplexer_1_out2), .clr(Reset));  // open: en
  Register #(.width(16)) r3 (.D(Write_Data), .Q(r3_q), .clk(demultiplexer_1_out3), .clr(Reset));  // open: en
  Register #(.width(16)) r4 (.D(Write_Data), .Q(r4_q), .clk(demultiplexer_1_out4), .clr(Reset));  // open: en
  Register #(.width(16)) r5 (.D(Write_Data), .Q(r5_q), .clk(demultiplexer_1_out5), .clr(Reset));  // open: en
  Register #(.width(16)) r6 (.D(Write_Data), .Q(r6_q), .clk(demultiplexer_1_out6), .clr(Reset));  // open: en
  Register #(.width(16)) r7 (.D(Write_Data), .Q(r3_q), .clk(demultiplexer_1_out7), .clr(Reset));  // open: en
  Multiplexer #(.select(3), .width(16), .enable("false")) multiplexer_1 (
    .in0(r0_q), .in1(r1_q), .in2(r2_q), .in3(r3_q), .in4(r4_q), .in5(r5_q), .in6(r6_q), .in7(r3_q),
    .out(Read_Reg_1_Output), .sel(Read_Reg_1));
  Multiplexer #(.select(3), .width(16), .enable("false")) multiplexer_2 (
    .in0(r0_q), .in1(r1_q), .in2(r2_q), .in3(r3_q), .in4(r4_q), .in5(r5_q), .in6(r6_q), .in7(r3_q),
    .out(Read_Reg_2_Output), .sel(Read_Reg_2));
endmodule
